// Logisim project alu.circ as structural Verilog: 1 circuit, main circuit main
module main (
  input  [31:0] X,
  input  [31:0] Y,
  input  [5:0] Switch__S,
  output Signed_Overflow,
  output [31:0] RESULT,
  output Equal
);

  wire and_2_out, and_3_out, and_4_out, and_5_out, checkOF, checkOF2, comparator_5_eq, comparator_6_eq,
       comparator_7_eq, or_5_out, overflow, xor_1_out, xor_2_out;
  wire [0:0] bitpal, slt, sltu;
  wire [31:0] add, addu, \and , lfsr, \or , sll, sra, srl, sub, subu;
  wire [31:31] shifter_4_out;

  Comparator #(.width(32)) comparator_1 (.a(X), .b(Y), .eq(Equal));  // open: gt, lt
  assign \and  = X & Y;  // AND_Gate and_1, 32 bits wide
  assign \or  = X | Y;  // OR_Gate or_1, 32 bits wide
  Adder #(.width(32)) adder_1 (.a(X), .b(Y), .out(addu));  // open: cin, cout
  Subtractor #(.width(32)) subtractor_1 (.a(X), .b(Y), .out(subu));  // open: bin, bout
  Comparator #(.width(32), .mode("unsigned")) comparator_2 (.a(X), .b(Y), .lt(sltu[0]));  // open: gt, eq
  Comparator #(.width(32)) comparator_3 (.a(X), .b(Y), .lt(slt[0]));  // open: gt, eq
  Shifter #(.width(32)) shifter_1 (.in(X), .\dist (Y[4:0]), .out(sll));
  Shifter #(.width(32), .shift("lr")) shifter_2 (.in(X), .\dist (Y[4:0]), .out(srl));
  Shifter #(.width(32), .shift("ar")) shifter_3 (.in(X), .\dist (Y[4:0]), .out(sra));
  Adder #(.width(32)) adder_2 (.a(X), .b(Y), .out(add));  // open: cin, cout
  Subtractor #(.width(32)) subtractor_2 (.a(X), .b(Y), .out(sub));  // open: bin, bout
  xor xor_1 (xor_1_out, X[0], X[2]);
  Shifter #(.width(32), .shift("lr")) shifter_4 (.in(X), .\dist (5'b00001), .out({shifter_4_out[31], lfsr[30:0]}));
  and and_2 (and_2_out, ~X[31], ~Y[31], add[31]);  // AND_Gate
  or or_2 (checkOF, and_2_out, and_3_out);
  and and_3 (and_3_out, X[31], Y[31], ~add[31]);  // AND_Gate
  and and_4 (and_4_out, ~X[31], ~Y[31], sub[31]);  // AND_Gate
  or or_3 (checkOF2, and_4_out, and_5_out);
  and and_5 (and_5_out, X[31], Y[31], ~sub[31]);  // AND_Gate
  xor xor_2 (xor_2_out, xor_1_out, X[3]);
  xor xor_3 (lfsr[31], xor_2_out, X[5]);
  Comparator #(.width(16)) comparator_4 (
    .a(X[15:0]),
    .b({X[16], X[17], X[18], X[19], X[20], X[21], X[22], X[23], X[24], X[25], X[26], X[27], X[28], X[29], X[30], X[31]}),
    .eq(bitpal[0]));  // open: gt, lt
  Comparator #(.width(6)) comparator_5 (.a(Switch__S), .b(6'b100000), .eq(comparator_5_eq));  // open: gt, lt
  Comparator #(.width(6)) comparator_6 (.a(Switch__S), .b(6'b100010), .eq(comparator_6_eq));  // open: gt, lt
  or or_4 (overflow, checkOF, checkOF2);
  or or_5 (or_5_out, comparator_5_eq, comparator_6_eq);
  Comparator #(.width(1)) comparator_7 (.a(or_5_out), .b(1'b1), .eq(comparator_7_eq));  // open: gt, lt
  // AND_Gate and_6 has open pins: in0=comparator_7_eq, in1=overflow, out=open
  Multiplexer #(.select(5)) multiplexer_1 (
    .in0(1'b0), .in2(1'b0), .in3(1'b0), .in16(checkOF), .in17(1'b0), .in18(checkOF2), .in19(1'b0),
    .in20(1'b0), .in21(1'b0), .in26(1'b0), .in27(1'b0), .in30(1'b0), .in31(1'b0), .out(Signed_Overflow),
    .sel({Switch__S[5], Switch__S[3:0]}));  // open: in1, in4, in5, in6, in7, in8, in9, in10, in11, in12, in13, in14, in15, in22, in23, in24, in25, in28, in29, en
  Multiplexer #(.select(5), .width(32)) multiplexer_2 (
    .in0(sll), .in2(srl), .in3(sra), .in16(add), .in17(addu), .in18(sub), .in19(subu), .in20(\and ),
    .in21(\or ), .in26({{31{1'b0}}, slt[0]}), .in27({{31{1'b0}}, sltu[0]}), .in30({{31{1'b0}}, bitpal[0]}),
    .in31(lfsr), .out(RESULT), .sel({Switch__S[5], Switch__S[3:0]}));  // open: in1, in4, in5, in6, in7, in8, in9, in10, in11, in12, in13, in14, in15, in22, in23, in24, in25, in28, in29, en

  // Other names for the same wires on the sheet: source1[31:0] = X; switch[5:0] = Switch__S; OF = Signed_Overflow;
  //   source2[31:0] = Y

  // Notes on the sheet:
  //   INPUTS to your circuit
  //   INPUT to your circuit
  //   DON'T CHANGE THE INPUTS AND OUTPUTS! IF YOU DO SO, YOU NEED TO MAKE SURE THE PINS ARE IN THE RIGHT PLACES!
  //   OUTPUTS of your circuit
endmodule
