// Logisim project cpu.circ as structural Verilog: 5 circuits, main circuit main
module main (
  input  [31:0] RS_READ_VALUE,
  input  [31:0] RT_READ_VALUE,
  input  [31:0] INSTRUCTION,
  input  CLOCK,
  input  RESET,
  output [31:0] t0,
  output [31:0] t1,
  output [31:0] t2,
  output [31:0] t3,
  output [4:0] RS,
  output [4:0] RT,
  output [4:0] Write_Register,
  output [31:0] RD_WRITE_VALUE,
  output RD_WRITE_ENABLE,
  output [23:0] FETCH_ADDRESS
);

  wire Access_Byte, ALU_signed_overflow, ALUSrc, and_2_out, and_3_out, and_4_out, BEQ, BNE, Branch,
       comparator_1_eq, comparator_2_eq, comparator_4_eq, comparator_5_eq, jal, jr, jump, lb, Lui, MemRead,
       MemtoReg, MemWrite, or_1_out, or_2_out, RegDst, RegWrite, s1eqs2, temp, temp_d, temp_s, temp_t,
       zeroExtOri;
  wire [1:0] multiplexer_7_out, multiplexer_8_out, multiplexer_9_out, multiplexer_10_out;
  wire [4:0] multiplexer_1_out, rd, shamt, subtractor_3_out, subtractor_4_out, subtractor_6_out;
  wire [5:0] ALU_OP, funct, opcode;
  wire [15:0] i_type_imm;
  wire [23:0] adder_1_out, adder_2_out, bit_extender_1_out, bit_extender_2_out, branchAddr, jumpAddr,
       multiplexer_3_out, multiplexer_4_out, subtractor_1_out, subtractor_2_out, subtractor_5_out;
  wire [25:0] j_type_imm;
  wire [31:0] ALU_rs_value, ALU_rt_value, bit_extender_3_out, bit_extender_4_out, bit_extender_5_out,
       bit_extender_6_out, bit_extender_7_out, bit_extender_8_out, MEM_data_mem_out, multiplexer_5_out,
       multiplexer_14_out, multiplexer_15_out, multiplexer_16_out, multiplexer_17_out, multiplexer_19_out,
       multiplexer_20_out, RegFile_read_data_2, Result, rs_temp, saved_inst, shifter_1_out;

  Multiplexer #(.width(5)) multiplexer_1 (.in0(RT), .in1(rd), .out(multiplexer_1_out), .sel(RegDst));  // open: en
  Multiplexer #(.width(5)) multiplexer_2 (
    .in0(multiplexer_1_out), .in1({5{1'b1}}), .out(Write_Register), .sel(jal));  // open: en
  and and_1 (RD_WRITE_ENABLE, RegWrite, ~temp);  // AND_Gate
  Adder #(.width(24)) adder_1 (.a(FETCH_ADDRESS), .b(24'h1), .out(adder_1_out));  // open: cin, cout
  or or_1 (or_1_out, jump, jr);
  Multiplexer #(.width(24)) multiplexer_3 (
    .in0(adder_1_out), .in1(jumpAddr), .out(multiplexer_3_out), .sel(or_1_out));  // open: en
  Multiplexer #(.width(24)) multiplexer_4 (
    .in0(multiplexer_3_out), .in1(branchAddr), .out(multiplexer_4_out), .sel(Branch));  // open: en
  Register #(.width(24)) register_1 (.D(multiplexer_4_out), .Q(FETCH_ADDRESS), .clk(CLOCK));  // open: en, clr
  // Probe on funct
  Decoder decoder (
    .in_1(saved_inst), .opcode(opcode), .rs(RS), .rt(RT), .rd(rd), .shamt(shamt), .funct(funct),
    .j_type_imm(j_type_imm), .i_type_imm(i_type_imm));  // open: RD_ENABLE, instruc_type
  Multiplexer #(.width(32)) multiplexer_5 (
    .in0(INSTRUCTION), .in1({32{1'b0}}), .out(multiplexer_5_out), .sel(or_2_out));  // open: en
  or or_2 (or_2_out, Branch, jump);
  Register #(.width(32)) register_2 (.D(multiplexer_5_out), .Q(saved_inst), .clk(CLOCK));  // open: en, clr
  and and_2 (and_2_out, s1eqs2, BEQ);
  and and_3 (and_3_out, ~s1eqs2, BNE);  // AND_Gate
  or or_3 (temp, temp_d, temp_t);
  or or_4 (Branch, and_2_out, and_3_out);
  Register_Comparator register_comparator_1 (.in_1(RS), .temp_register(temp_s));
  Register_Comparator register_comparator_2 (.in_1(RT), .temp_register(temp_t));
  Register_Comparator register_comparator_3 (.in_1(rd), .temp_register(temp_d));
  ALU_Control alu_control_1 (.opcode(opcode), .in_2(funct), .ALU_OP(ALU_OP));
  opcode_control_unit Opcode_Control (
    .opcode(opcode), .RegDst(RegDst), .ALUSrc(ALUSrc), .MemtoReg(MemtoReg), .RegWrite(RegWrite),
    .MemRead(MemRead), .MemWrite(MemWrite), .BNE(BNE), .Branch(BEQ), .Jump(jump), .AccessByte(Access_Byte),
    .Lui(Lui), .lb(lb));
  assign bit_extender_1_out = {{8{i_type_imm[15]}}, i_type_imm};  // Bit_Extender bit_extender_1
  Subtractor #(.width(24)) subtractor_1 (
    .a(j_type_imm[23:0]), .b(24'h100000), .out(subtractor_1_out));  // open: bin, bout
  Adder #(.width(24)) adder_2 (.a(bit_extender_1_out), .b(FETCH_ADDRESS), .out(adder_2_out));  // open: cin, cout
  Multiplexer #(.width(24)) multiplexer_6 (
    .in0(subtractor_1_out), .in1(adder_2_out), .out(branchAddr), .sel(Branch));  // open: en
  Subtractor #(.width(24)) subtractor_2 (
    .a(j_type_imm[23:0]), .b(24'h100000), .out(subtractor_2_out));  // open: bin, bout
  Bit_Extender #(.in_width(32), .out_width(24), .\type ("sign")) bit_extender_2 (
    .in(ALU_rs_value), .out(bit_extender_2_out));
  Multiplexer #(.width(2)) multiplexer_7 (
    .in1(subtractor_3_out[1:0]), .out(multiplexer_7_out), .sel(temp_t));  // open: in0, en
  Subtractor #(.width(5)) subtractor_3 (.a(RT), .b(5'b01000), .out(subtractor_3_out));  // open: bin, bout
  Multiplexer #(.width(2)) multiplexer_8 (
    .in1(subtractor_4_out[1:0]), .out(multiplexer_8_out), .sel(temp_d));  // open: in0, en
  Subtractor #(.width(5)) subtractor_4 (.a(rd), .b(5'b01000), .out(subtractor_4_out));  // open: bin, bout
  Subtractor #(.width(24)) subtractor_5 (
    .a(bit_extender_2_out), .b(24'h100000), .out(subtractor_5_out));  // open: bin, bout
  Multiplexer #(.width(2)) multiplexer_9 (
    .in1(subtractor_6_out[1:0]), .out(multiplexer_9_out), .sel(temp_s));  // open: in0, en
  Subtractor #(.width(5)) subtractor_6 (.a(RS), .b(5'b01000), .out(subtractor_6_out));  // open: bin, bout
  Multiplexer #(.width(2)) multiplexer_10 (
    .in0(multiplexer_7_out), .in1(multiplexer_8_out), .out(multiplexer_10_out), .sel(RegDst));  // open: en
  Multiplexer #(.width(24)) multiplexer_11 (
    .in0(subtractor_2_out), .in1(subtractor_5_out), .out(jumpAddr), .sel(jr));  // open: en
  // Probe on jumpAddr
  Comparator #(.width(6)) comparator_1 (.a(opcode), .b({6{1'b0}}), .eq(comparator_1_eq));  // open: gt, lt
  Comparator #(.width(6)) comparator_2 (.a(funct), .b(6'b001000), .eq(comparator_2_eq));  // open: gt, lt
  Comparator #(.width(6)) comparator_3 (.a(opcode), .b(6'b000011), .eq(jal));  // open: gt, lt
  Comparator #(.width(6)) comparator_4 (.a(opcode), .b(6'b001101), .eq(comparator_4_eq));  // open: gt, lt
  Comparator #(.width(6)) comparator_5 (.a(ALU_OP), .b(6'b100101), .eq(comparator_5_eq));  // open: gt, lt
  regfile_main RegFile (
    .Read_register_1(multiplexer_9_out), .Read_register_2(multiplexer_7_out),
    .write_register(multiplexer_10_out), .write_data(RD_WRITE_VALUE), .t0_Value(t0), .t1_Value(t1),
    .t2_Value(t2), .t3_Value(t3), .RegWrite(and_4_out), .clock(CLOCK), .Read_Data_1(rs_temp),
    .Read_Data_2(RegFile_read_data_2));
  and and_4 (and_4_out, temp, RegWrite);
  and and_5 (jr, comparator_1_eq, comparator_2_eq);
  and and_6 (zeroExtOri, comparator_4_eq, comparator_5_eq);
  Multiplexer #(.width(32)) multiplexer_12 (
    .in0(RS_READ_VALUE), .in1(rs_temp), .out(ALU_rs_value), .sel(temp_s));  // open: en
  Multiplexer #(.width(32)) multiplexer_13 (
    .in0(RT_READ_VALUE), .in1(RegFile_read_data_2), .out(ALU_rt_value), .sel(temp_t));  // open: en
  assign bit_extender_3_out = {{16{i_type_imm[15]}}, i_type_imm};  // Bit_Extender bit_extender_3
  Multiplexer #(.width(32)) multiplexer_14 (
    .in0(ALU_rt_value), .in1(bit_extender_3_out), .out(multiplexer_14_out), .sel(ALUSrc));  // open: en
  Multiplexer #(.width(32)) multiplexer_15 (
    .in0(multiplexer_14_out), .in1(bit_extender_4_out), .out(multiplexer_15_out), .sel(zeroExtOri));  // open: en
  alu_main ALU (
    .Switch__S(ALU_OP), .X(ALU_rs_value), .Equal(s1eqs2), .RESULT(Result),
    .Signed_Overflow(ALU_signed_overflow), .Y(multiplexer_15_out));
  LED led_1 (.in(ALU_signed_overflow));
  assign bit_extender_4_out = {{16{1'b0}}, i_type_imm};  // Bit_Extender bit_extender_4
  assign bit_extender_5_out = {{16{1'b0}}, i_type_imm};  // Bit_Extender bit_extender_5
  Shifter #(.width(32)) shifter_1 (.in(bit_extender_5_out), .\dist (5'b10000), .out(shifter_1_out));
  mem_main MEM (
    .Data_Mem_Addr(Result), .Data_Mem_In(ALU_rt_value), .ACCESS_BYTE(Access_Byte), .MEM_WRITE(MemWrite),
    .CLOCK(CLOCK), .Data_Mem_Out(MEM_data_mem_out));
  assign bit_extender_6_out = {{8{1'b0}}, FETCH_ADDRESS};  // Bit_Extender bit_extender_6
  Multiplexer #(.width(32)) multiplexer_16 (
    .in0(Result), .in1(shifter_1_out), .out(multiplexer_16_out), .sel(Lui));  // open: en
  Multiplexer #(.width(32)) multiplexer_17 (
    .in0(multiplexer_16_out), .in1(multiplexer_19_out), .out(multiplexer_17_out), .sel(MemtoReg));  // open: en
  Multiplexer #(.width(32)) multiplexer_18 (
    .in0(multiplexer_17_out), .in1(bit_extender_6_out), .out(RD_WRITE_VALUE), .sel(jal));  // open: en
  assign bit_extender_7_out = {{24{MEM_data_mem_out[7]}}, MEM_data_mem_out[7:0]};  // Bit_Extender bit_extender_7
  assign bit_extender_8_out = {{24{1'b0}}, MEM_data_mem_out[7:0]};  // Bit_Extender bit_extender_8
  Multiplexer #(.width(32)) multiplexer_19 (
    .in0(MEM_data_mem_out), .in1(multiplexer_20_out), .out(multiplexer_19_out), .sel(Access_Byte));  // open: en
  Multiplexer #(.width(32)) multiplexer_20 (
    .in0(bit_extender_8_out), .in1(bit_extender_7_out), .out(multiplexer_20_out), .sel(lb));  // open: en

  // Other names for the same wires on the sheet: CLK = CLOCK; instruc[31:0] = INSTRUCTION; PC[23:0] = FETCH_ADDRESS;
  //   PC_inc[23:0] = FETCH_ADDRESS; rs_value[31:0] = RS_READ_VALUE; RST = RESET; rt_value[31:0] = RT_READ_VALUE;
  //   Write_Value[31:0] = RD_WRITE_VALUE

  // Notes on the sheet:
  //   Feel free to move these components
  //   These are outputs/inputs from run.circ
  //   Bit Offset Counter
  //   These are outputs to run.circ
endmodule

module Decoder (
  input  [31:0] in_1,
  output [5:0] opcode,
  output [4:0] rs,
  output [4:0] rt,
  output [4:0] rd,
  output [4:0] shamt,
  output [5:0] funct,
  output [25:0] j_type_imm,
  output [15:0] i_type_imm,
  output RD_ENABLE,
  output [1:0] instruc_type
);

  wire decoder_1_out1, decoder_1_out2, decoder_1_out3, decoder_1_out8, decoder_1_out9, decoder_1_out10,
       decoder_2_out2, decoder_2_out3, I_type, J_type, R_or_J;

  Decoder_part #(.select(4), .enable("false")) decoder_1 (
    .out0(R_or_J), .out1(decoder_1_out1), .out2(decoder_1_out2), .out3(decoder_1_out3),
    .out8(decoder_1_out8), .out9(decoder_1_out9), .out10(decoder_1_out10), .sel(in_1[31:28]));  // open: out4, out5, out6, out7, out11, out12, out13, out14, out15
  Decoder_part #(.select(2), .enable("false")) decoder_2 (
    .out0(RD_ENABLE), .out2(decoder_2_out2), .out3(decoder_2_out3), .sel(in_1[27:26]));  // open: out1
  or or_1 (J_type, decoder_2_out2, decoder_2_out3);
  or or_2 (I_type, decoder_1_out1, decoder_1_out2, decoder_1_out3, decoder_1_out8, decoder_1_out9, decoder_1_out10);

  assign funct = in_1[5:0];
  assign i_type_imm = in_1[15:0];
  assign j_type_imm = in_1[25:0];
  assign opcode = in_1[31:26];
  assign rd = in_1[15:11];
  assign rs = in_1[25:21];
  assign rt = in_1[20:16];
  assign shamt = in_1[10:6];

  // Other names for the same wires on the sheet: i_imm[15:0] = in_1[15:0]; instruc[31:0] = in_1;
  //   j_imm[25:0] = in_1[25:0]; instr_type[1:0] = instruc_type; R_type = RD_ENABLE

  // Notes on the sheet:
  //   R=0 I=1 J=2
endmodule

module opcode_control_unit (
  input  [5:0] opcode,
  output RegDst,
  output ALUSrc,
  output MemtoReg,
  output RegWrite,
  output MemRead,
  output MemWrite,
  output BNE,
  output Branch,
  output Jump,
  output AccessByte,
  output Lui,
  output lb
);

  wire addiu_out, andi_out, bitpal_out, j_out, jal_out, lbu_out, lfsr_out, lw_out, ori_out, R_type_out;

  and R_type (R_type_out, ~opcode[5], ~opcode[4], ~opcode[3], ~opcode[2], ~opcode[1], ~opcode[0]);  // AND_Gate
  and bitpal (bitpal_out, opcode[5], opcode[4], opcode[3], opcode[2], opcode[1], ~opcode[0]);  // AND_Gate
  and lw (lw_out, opcode[5], ~opcode[4], ~opcode[3], ~opcode[2], opcode[1], opcode[0]);  // AND_Gate
  and lfsr (lfsr_out, opcode[5], opcode[4], opcode[3], opcode[2], opcode[1], opcode[0]);
  and sw (MemWrite, opcode[5], ~opcode[4], opcode[3], ~opcode[2], opcode[1], opcode[0]);  // AND_Gate
  and j (j_out, ~opcode[5], ~opcode[4], ~opcode[3], ~opcode[2], opcode[1], ~opcode[0]);  // AND_Gate
  and beq (Branch, ~opcode[5], ~opcode[4], ~opcode[3], opcode[2], ~opcode[1], ~opcode[0]);  // AND_Gate
  and jal (jal_out, ~opcode[5], ~opcode[4], ~opcode[3], ~opcode[2], opcode[1], opcode[0]);  // AND_Gate
  and u_bne (BNE, ~opcode[5], ~opcode[4], ~opcode[3], opcode[2], ~opcode[1], opcode[0]);  // AND_Gate
  and u_lb (lb, opcode[5], ~opcode[4], ~opcode[3], ~opcode[2], ~opcode[1], ~opcode[0]);  // AND_Gate
  and ori (ori_out, ~opcode[5], ~opcode[4], opcode[3], opcode[2], ~opcode[1], opcode[0]);  // AND_Gate
  and lbu (lbu_out, opcode[5], ~opcode[4], ~opcode[3], opcode[2], ~opcode[1], ~opcode[0]);  // AND_Gate
  and u_lui (Lui, ~opcode[5], ~opcode[4], opcode[3], opcode[2], opcode[1], opcode[0]);  // AND_Gate
  and addiu (addiu_out, ~opcode[5], ~opcode[4], opcode[3], ~opcode[2], ~opcode[1], opcode[0]);  // AND_Gate
  and andi (andi_out, ~opcode[5], ~opcode[4], opcode[3], opcode[2], ~opcode[1], ~opcode[0]);  // AND_Gate
  or or_1 (RegDst, bitpal_out, R_type_out, lfsr_out);
  or or_2 (ALUSrc, lb, ori_out, lbu_out, lw_out, MemWrite, Lui, addiu_out, andi_out);
  or or_3 (MemRead, Lui, lbu_out, lw_out, lb);
  or or_4 (Jump, j_out, jal_out);
  or or_5 (AccessByte, lbu_out, lb);
  or or_6 (MemtoReg, lw_out, lb, lbu_out);
  or or_7 (RegWrite, lb, bitpal_out, ori_out, Lui, R_type_out, lw_out, lbu_out, addiu_out, andi_out, lfsr_out);
endmodule

module ALU_Control (
  input  [5:0] opcode,
  input  [5:0] in_2,
  output [5:0] ALU_OP
);

  wire addiu_out, andi_out, lb_out, lbu_out, lui_out, lw_out, or_1_out, ori_out, sw_out;
  wire [5:0] undriven;

  and ori (ori_out, ~opcode[5], ~opcode[4], opcode[3], opcode[2], ~opcode[1], opcode[0]);  // AND_Gate
  Multiplexer #(.width(6)) multiplexer_1 (.in0(undriven), .in1(6'b100101), .out(ALU_OP), .sel(ori_out));  // open: en
  and lui (lui_out, ~opcode[5], ~opcode[4], opcode[3], opcode[2], opcode[1], opcode[0]);  // AND_Gate
  and andi (andi_out, ~opcode[5], ~opcode[4], opcode[3], opcode[2], ~opcode[1], ~opcode[0]);  // AND_Gate
  Multiplexer #(.width(6)) multiplexer_2 (.in1({6{1'b0}}), .out(ALU_OP), .sel(lui_out));  // open: in0, en
  Multiplexer #(.width(6)) multiplexer_3 (.in1(6'b100100), .out(ALU_OP), .sel(andi_out));  // open: in0, en
  and lw (lw_out, opcode[5], ~opcode[4], ~opcode[3], ~opcode[2], opcode[1], opcode[0]);  // AND_Gate
  Multiplexer #(.width(6)) multiplexer_4 (.in1(6'b100000), .out(ALU_OP), .sel(lw_out));  // open: in0, en
  and sw (sw_out, opcode[5], ~opcode[4], opcode[3], ~opcode[2], opcode[1], opcode[0]);  // AND_Gate
  Multiplexer #(.width(6)) multiplexer_5 (.in1(6'b100000), .out(ALU_OP), .sel(sw_out));  // open: in0, en
  and addiu (addiu_out, ~opcode[5], ~opcode[4], opcode[3], ~opcode[2], ~opcode[1], opcode[0]);  // AND_Gate
  and lbu (lbu_out, opcode[5], ~opcode[4], ~opcode[3], opcode[2], ~opcode[1], ~opcode[0]);  // AND_Gate
  Multiplexer #(.width(6)) multiplexer_6 (.in1(6'b100000), .out(ALU_OP), .sel(addiu_out));  // open: in0, en
  Multiplexer #(.width(6)) multiplexer_7 (.in1(6'b100000), .out(ALU_OP), .sel(lbu_out));  // open: in0, en
  and lb (lb_out, opcode[5], ~opcode[4], ~opcode[3], ~opcode[2], ~opcode[1], ~opcode[0]);  // AND_Gate
  Multiplexer #(.width(6)) multiplexer_8 (.in1(6'b100000), .out(ALU_OP), .sel(lb_out));  // open: in0, en
  or or_1 (or_1_out, ori_out, lui_out, andi_out, lw_out, sw_out, addiu_out, lbu_out, lb_out);
  Multiplexer #(.width(6)) multiplexer_9 (.in0(in_2), .out(ALU_OP), .sel(or_1_out));  // open: in1, en

  // Other names for the same wires on the sheet: funct[5:0] = in_2

  // Notes on the sheet:
  //   or
  //   sll
  //   and
  //   add
endmodule

module Register_Comparator (
  input  [4:0] in_1,
  output temp_register
);

  wire comparator_1_lt, comparator_2_lt;

  Comparator #(.width(5), .mode("unsigned")) comparator_1 (
    .a(5'b00111), .b(in_1), .lt(comparator_1_lt));  // open: gt, eq
  Comparator #(.width(5), .mode("unsigned")) comparator_2 (
    .a(in_1), .b(5'b01100), .lt(comparator_2_lt));  // open: gt, eq
  and and_1 (temp_register, comparator_1_lt, comparator_2_lt);
endmodule
