// Logisim project regfile.circ as structural Verilog: 2 circuits, main circuit main
module main (
  input  [1:0] Read_register_1,
  input  [1:0] Read_register_2,
  input  [1:0] write_register,
  input  [31:0] write_data,
  input  RegWrite,
  input  clock,
  output [31:0] t0_Value,
  output [31:0] t1_Value,
  output [31:0] t2_Value,
  output [31:0] t3_Value,
  output [31:0] Read_Data_1,
  output [31:0] Read_Data_2
);

  wire Wt0, Wt1, Wt2, Wt3;

  Write_Compare write_compare_1 (.in_1(write_data), .in_2(Wt0), .in_3(clock), .out_4(t0_Value));
  Write_Compare write_compare_2 (.in_1(write_data), .in_2(Wt1), .in_3(clock), .out_4(t1_Value));
  Demultiplexer #(.select(2)) demultiplexer_1 (
    .out0(Wt0), .out1(Wt1), .out2(Wt2), .out3(Wt3), .in(RegWrite), .sel(write_register));  // open: en
  Write_Compare write_compare_3 (.in_1(write_data), .in_2(Wt2), .in_3(clock), .out_4(t2_Value));
  Write_Compare write_compare_4 (.in_1(write_data), .in_2(Wt3), .in_3(clock), .out_4(t3_Value));
  Multiplexer #(.select(2), .width(32)) multiplexer_1 (
    .in0(t0_Value), .in1(t1_Value), .in2(t2_Value), .in3(t3_Value), .out(Read_Data_1), .sel(Read_register_1));  // open: en
  Multiplexer #(.select(2), .width(32)) multiplexer_2 (
    .in0(t0_Value), .in1(t1_Value), .in2(t2_Value), .in3(t3_Value), .out(Read_Data_2), .sel(Read_register_2));  // open: en

  // Other names for the same wires on the sheet: CLK = clock; RR1[1:0] = Read_register_1; RR2[1:0] = Read_register_2;
  //   WR[1:0] = write_register; Write_Value[31:0] = write_data

  // Notes on the sheet:
  //   These are INPUTS to the circuit
  //   These are INPUTS to the circuit
  //   DO NOT CHANGE THE LOCATIONS OF THE INPUTS/OUTPUTS! IF YOU DO SO, YOU NEED TO MAKE SURE THE PINS ARE AT THE RIGHT PLACE!
  //   These are OUTPUTS to the circuit
  //   Yet again, the clock is not an actual clock, but an input, one that will be driven from a higher circuit
  //   These are OUTPUTS to the circuit
endmodule

module Write_Compare (
  input  [31:0] in_1,
  input  in_2,
  input  in_3,
  output [31:0] out_4
);

  Register #(.width(32)) register_1 (.D(in_1), .en(in_2), .Q(out_4), .clk(in_3));  // open: clr
endmodule
