// Logisim project mem.circ as structural Verilog: 1 circuit, main circuit main
module main (
  input  [31:0] Data_Mem_Addr,
  input  [31:0] Data_Mem_In,
  input  ACCESS_BYTE,
  input  MEM_WRITE,
  input  CLOCK,
  output [31:0] Data_Mem_Out
);

  wire comparator_1_eq, comparator_3_eq, Load, not_1_out;
  wire [31:0] controlled_buffer_1_out, shifter_1_out, subtractor_1_out;

  Comparator #(.width(1), .mode("unsigned")) comparator_1 (
    .a(1'b1), .b(ACCESS_BYTE), .eq(comparator_1_eq));  // open: gt, lt
  Comparator #(.width(1), .mode("unsigned")) comparator_2 (
    .a(comparator_1_eq), .b(comparator_3_eq), .eq(Load));  // open: gt, lt
  Comparator #(.width(1), .mode("unsigned")) comparator_3 (
    .a(MEM_WRITE), .b(1'b0), .eq(comparator_3_eq));  // open: gt, lt
  Subtractor #(.width(32)) subtractor_1 (
    .a(Data_Mem_Addr), .b(32'h10010000), .out(subtractor_1_out));  // open: bin, bout
  not not_1 (not_1_out, MEM_WRITE);
  assign controlled_buffer_1_out = MEM_WRITE ? Data_Mem_In : 32'bz;  // Controlled_Buffer controlled_buffer_1
  RAM #(.addrWidth(24), .dataWidth(32)) ram_1 (
    .addr(subtractor_1_out[25:2]), .data(controlled_buffer_1_out), .sel(1'b1), .clk(CLOCK), .ld(not_1_out),
    .clr(1'b0));
  Shifter #(.width(32), .shift("lr")) shifter_1 (.in(controlled_buffer_1_out), .\dist (5'b11000), .out(shifter_1_out));
  Multiplexer #(.width(32)) multiplexer_1 (
    .in0(controlled_buffer_1_out), .in1(shifter_1_out), .out(Data_Mem_Out), .sel(Load));  // open: en

  // Other names for the same wires on the sheet: AB = ACCESS_BYTE; CLK = CLOCK; MW = MEM_WRITE;
  //   output[31:0] = Data_Mem_Out

  // Notes on the sheet:
  //   These are INPUTS to the circuit
  //   These are INPUTS to the circuit
  //   DO NOT CHANGE THE LOCATIONS OF THE INPUTS/OUTPUTS! IF YOU DO SO, YOU NEED TO MAKE SURE THE PINS ARE AT THE RIGHT PLACE!
  //   Yet again, the clock is not an actual clock, but an input, one that will be driven from a higher circuit
  //   This is an OUTPUT to the circuit
endmodule
