// Logisim project regfile.circ as structural Verilog: 2 circuits, main circuit main
module main (
  input  [1:0] Read_register_1,
  input  [1:0] Read_register_2,
  input  [1:0] write_register,
  input  [31:0] write_data,
  input  RegWrite,
  input  clock,
  output [31:0] t0_Value,
  output [31:0] t1_Value,
  output [31:0] t2_Value,
  output [31:0] t3_Value,
  output [31:0] Read_Data_1,
  output [31:0] Read_Data_2
);

  wire [31:0] multiplexer_1_out, Wt0, Wt1, Wt2, Wt3;

  Write_Compare write_compare_1 (
    .Reg_num(2'b00), .WR(write_register), .CLK(clock), .Write_Register_val(Wt0), .out_5(t0_Value));
  Write_Compare write_compare_2 (
    .Reg_num(2'b01), .WR(write_register), .CLK(clock), .Write_Register_val(Wt1), .out_5(t1_Value));
  Multiplexer #(.width(32)) multiplexer_1 (.in1(write_data), .out(multiplexer_1_out), .sel(RegWrite));  // open: in0, en
  Demultiplexer #(.select(2), .width(32)) demultiplexer_1 (
    .out0(Wt0), .out1(Wt1), .out2(Wt2), .out3(Wt3), .in(multiplexer_1_out), .sel(write_register));  // open: en
  Write_Compare write_compare_3 (
    .Reg_num(2'b10), .WR(write_register), .CLK(clock), .Write_Register_val(Wt2), .out_5(t2_Value));
  Write_Compare write_compare_4 (
    .Reg_num(2'b11), .WR(write_register), .CLK(clock), .Write_Register_val(Wt3), .out_5(t3_Value));
  Multiplexer #(.select(2), .width(32)) multiplexer_2 (
    .in0(t0_Value), .in1(t1_Value), .in2(t2_Value), .in3(t3_Value), .out(Read_Data_1), .sel(Read_register_1));  // open: en
  Multiplexer #(.select(2), .width(32)) multiplexer_3 (
    .in0(t0_Value), .in1(t1_Value), .in2(t2_Value), .in3(t3_Value), .out(Read_Data_2), .sel(Read_register_2));  // open: en

  // Other names for the same wires on the sheet: CLK = clock; RR1[1:0] = Read_register_1; RR2[1:0] = Read_register_2;
  //   WR[1:0] = write_register

  // Notes on the sheet:
  //   These are INPUTS to the circuit
  //   These are INPUTS to the circuit
  //   DO NOT CHANGE THE LOCATIONS OF THE INPUTS/OUTPUTS! IF YOU DO SO, YOU NEED TO MAKE SURE THE PINS ARE AT THE RIGHT PLACE!
  //   These are OUTPUTS to the circuit
  //   Yet again, the clock is not an actual clock, but an input, one that will be driven from a higher circuit
  //   These are OUTPUTS to the circuit
endmodule

module Write_Compare (
  input  [1:0] Reg_num,
  input  [1:0] WR,
  input  CLK,
  input  [31:0] Write_Register_val,
  output [31:0] out_5
);

  wire comparator_1_eq;

  Comparator #(.width(2)) comparator_1 (.a(Reg_num), .b(WR), .eq(comparator_1_eq));  // open: gt, lt
  Register #(.width(32)) register_1 (.D(Write_Register_val), .en(comparator_1_eq), .Q(out_5), .clk(CLK));  // open: clr
endmodule
